// Digital circuit Main.dig as structural Verilog
module Main (
  input  clk
);

  wire address_register_1_p1, address_register_1_p3, address_register_2_p3, address_register_3_p3,
       address_register_4_p3, address_register_5_p3, address_register_5_p6, bus_control_p3, bus_control_p4,
       bus_control_p7, bus_control_p8, Stage_1_p4, stage_2_1_p3;
  wire [1:0] bus_control_p6, Stage_1_p8;
  wire [2:0] address_register_5_p7;
  wire [3:0] address_register_3_p5, address_register_4_p5, address_register_5_p5, bus_control_p10,
       bus_control_p11, Stage_1_p6;
  wire [6:0] bus_control_p9;
  wire [7:0] gpr_1_lhs, gpr_1_main, gpr_1_rhs, memory_1_mem, stage_2_1_p1;
  wire [15:0] address_register_1_p2;

  // Address_Register address_register_1: pin names not known; wires that end beside it: address_register_1_p1, address_register_1_p2, address_register_1_p3
  // Address_Register address_register_2: pin names not known; wires that end beside it: address_register_1_p1, address_register_1_p2, address_register_2_p3
  // Address_Register address_register_3: pin names not known; wires that end beside it: address_register_1_p1, address_register_1_p2, address_register_3_p3, address_register_3_p3, address_register_3_p5
  // Address_Register address_register_4: pin names not known; wires that end beside it: address_register_1_p1, address_register_1_p2, address_register_4_p3, address_register_4_p3, address_register_4_p5
  // Address_Register address_register_5: pin names not known; wires that end beside it: address_register_1_p1, address_register_1_p2, address_register_5_p3, address_register_5_p3, address_register_5_p5, address_register_5_p6, address_register_5_p7
  // Tranfer_Register tranfer_register_1: pin names not known; wires that end beside it: address_register_1_p1, address_register_1_p2, address_register_5_p6
  Memory memory_1 (.ADDR(address_register_1_p2), .Control(address_register_5_p5), .MEM(memory_1_mem));
  // Bus_Control bus_control: pin names not known; wires that end beside it: address_register_1_p3, address_register_2_p3, bus_control_p3, bus_control_p4, {clk, stage_2_1_p1[6]}, bus_control_p6, bus_control_p7, bus_control_p8, bus_control_p9, bus_control_p10, bus_control_p11
  GPR gpr_1 (.RHS(gpr_1_rhs), .LHS(gpr_1_lhs), .MAIN(gpr_1_main), .Control(bus_control_p10));  // open: I
  GPR gpr_2 (.RHS(gpr_1_rhs), .LHS(gpr_1_lhs), .MAIN(gpr_1_main), .Control(bus_control_p11));  // open: I
  GPR gpr_3 (.RHS(gpr_1_rhs), .LHS(gpr_1_lhs), .MAIN(gpr_1_main), .Control(address_register_3_p5));  // open: I
  GPR gpr_4 (.RHS(gpr_1_rhs), .LHS(gpr_1_lhs), .MAIN(gpr_1_main), .Control(address_register_4_p5));  // open: I
  Constant_Register constant_register_1 (.MEM(memory_1_mem), .MAIN(gpr_1_main), .Control(address_register_5_p7));
  Memory_Bridge memory_bridge_1 (.MAIN(gpr_1_main), .Control(address_register_5_p5));  // open: MEM
  ALU alu_1 (
    .Assert_Main(bus_control_p9[0]), .FLAGS(stage_2_1_p1[4:0]), .LHS(gpr_1_lhs), .RHS(gpr_1_rhs),
    .MAIN(gpr_1_lhs), .Clock(clk), .Control(Stage_1_p6));
  // Stage_2 stage_2_1: pin names not known; wires that end beside it: stage_2_1_p1, clk, stage_2_1_p3, bus_control_p3, bus_control_p6[1], bus_control_p8, Stage_1_p8[1], stage_2_1_p1[5]
  // Stage_1 Stage_1: pin names not known; wires that end beside it: stage_2_1_p1, clk, stage_2_1_p3, Stage_1_p4, bus_control_p7, Stage_1_p6, bus_control_p4, Stage_1_p8[0], Stage_1_p8
  // Fetch Fetch: pin names not known; wires that end beside it: gpr_1_main, memory_1_mem, stage_2_1_p1, clk, Stage_1_p4, bus_control_p6[0], Stage_1_p8
  Button button_1 (.out(stage_2_1_p1[6]));
endmodule
